# Fritzing sketch coil_drive (saved by Fritzing 0.9.2b)
breadboards: 1

parts:
  P-Channel_MOSFET = Basic FET P-Channel [package="TO220 [THT]"]
  N-Channel_MOSFET = Basic FET N-Channel [package="TO220 [THT]"]
  R1 = Resistor [tolerance=±5% resistance=10k package=THT]
  R2 = Resistor [tolerance=±5% resistance=10k package=THT]

nets:
  N1: P-Channel_MOSFET.gate, N-Channel_MOSFET.drain, R1.Pin_0
  Coil Pulse: P-Channel_MOSFET.drain
  18V: P-Channel_MOSFET.source, R1.Pin_1
  3-6V Pulse: N-Channel_MOSFET.gate, R2.Pin_0
  GND: N-Channel_MOSFET.source, R2.Pin_1
